# Fritzing sketch Control Remoto Mitsubishi (saved by Fritzing 0.9.3b)
breadboards: 1

parts:
  Part1 = Arduino Uno (Rev3)
  LED2 = LED - 5mm [color="Infrared (940nm)" package="5 mm [THT]"]
  T2 = LM35 Temperature Sensor [package="TO92 [THT]"]

nets:
  N1: Part1.A0, T2.Vout
  GND: Part1.GND, LED2.cathode, T2.GND
  N2: Part1.D3_PWM, LED2.anode
  N3: Part1.3V3, T2.+Vs
