# Fritzing sketch Mitsubishi-IR-Arduino-Nano (saved by Fritzing 0.9.3b)

parts:
  T2 = LM35 Temperature Sensor [package="TO92 [THT]"]
  Part2 = Arduino Nano (Rev3.0)
  IR1 = TSOP312.., 314.. [package=THT]

nets:
  N1: T2.+Vs, Part2.A3, Part2.3V3
  N2: T2.Vout, Part2.A0
  GND: T2.GND, Part2.GND, IR1.GND
  N3: Part2.D2, Part2.D3, IR1.Data
  N4: Part2.RESET, Part2.5V, IR1.Vs
